# Fritzing sketch distance-sensor-02 (saved by Fritzing 0.9.2b)
breadboards: 1

parts:
  U2 = HC-SR04 [chip_label=IC package="SIP (Single Inline) [THT]"]
  Part1 = Arduino Uno (Rev3)

nets:
  VCC: U2.Vcc, Part1.5V
  GND: U2.GND, Part1.GND

custom parts:
  HC-SR04: HC-SR04 ultrasound distance sensor
