# Fritzing sketch led (saved by Fritzing 0.9.2b)
breadboards: 1

parts:
  Part1 = Photon
  LED1 = smd LED [color="Red (633nm)" package="0805 [SMD]"]

nets:
  N1: Part1.GND, LED1.cathode
  N2: Part1.D7, LED1.anode
