# Fritzing sketch line-sensor (saved by Fritzing 0.9.2b)

parts:
  TCRT1 = TCRT5000 digital module [part_number=151608]
  Part1 = Arduino Uno (Rev3)

nets:
  VCC: TCRT1.VCC, Part1.5V
  GND: TCRT1.GND, Part1.GND
  N1: TCRT1.DO2, Part1.A5/SCL

custom parts:
  TCRT5000 digital module: breakout board for TCRT5000 module, convert analog to digital - Uses TCRT5000 infrared reflectance sensor - Detection distance: 1mm~8mm - Focus distance: 2.5mm - Working voltage: 3.3V~12V - Uses wide voltage LM393 comparator - With multi-turn precision potentiometer to adjust the sensitivity - Current: > 15mA - Output type: Digital switch output (0, 1) - Suitable for watt-hour meter pulse data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
